// Logisim project ex2.circ as structural Verilog: 6 circuits, main circuit AND2
module AND2 (
  input  A,
  input  B,
  output RESULT
);

  and and_1 (RESULT, A, B);

  // Notes on the sheet:
  //   Sample Circuit
endmodule

module NAND2 (
  input  A,
  input  B,
  output RESULT
);

  wire tmp;

  and and_1 (tmp, A, B);
  not not_1 (RESULT, tmp);
endmodule

module NOR2 (
  input  A,
  input  B,
  output RESULT
);

  wire tmp;

  or or_1 (tmp, A, B);
  not not_1 (RESULT, tmp);
endmodule

module XOR2 (
  input  A,
  input  B,
  output RESULT
);

  wire left, notA, notB, right;

  not not_1 (notA, A);
  or or_1 (RESULT, left, right);
  not not_2 (notB, B);
  and and_1 (left, A, notB);
  and and_2 (right, notA, B);
endmodule

module MUX2 (
  input  A,
  input  B,
  input  SEL,
  output RESULT
);

  wire left, notSel, right;

  not not_1 (notSel, SEL);
  and and_1 (left, A, notSel);
  and and_2 (right, B, SEL);
  or or_1 (RESULT, left, right);
endmodule

module MUX4 (
  input  A,
  input  B,
  input  C,
  input  D,
  input  SEL0,
  input  SEL1,
  output RESULT
);

  wire hi, lo, n0, n1, p0, p1, p2, p3, t0, t1, t2, t3;

  not not_1 (n0, SEL0);
  and and_1 (t1, B, SEL0);
  and and_2 (t3, D, SEL0);
  or or_1 (RESULT, lo, hi);
  not not_2 (n1, SEL1);
  and and_3 (p1, t1, n1);
  and and_4 (p3, t3, SEL1);
  and and_5 (t0, A, n0);
  and and_6 (t2, C, n0);
  or or_2 (lo, p0, p1);
  and and_7 (p0, t0, n1);
  and and_8 (p2, t2, SEL1);
  or or_3 (hi, p2, p3);
endmodule
