// Logisim project ex3.circ as structural Verilog: 1 circuit, main circuit AddMachine
module AddMachine (
  input  clk,
  output [7:0] ADD_OUT,
  output [7:0] REG_OUT
);

  wire adder_1_cout;

  Adder #(.width(8)) adder_1 (.a(REG_OUT), .b(8'h1), .out(ADD_OUT), .cout(adder_1_cout));  // open: cin
  Register #(.width(8)) register_1 (.D(ADD_OUT), .clk(clk), .Q(REG_OUT));  // open: en, clr
  // also tied to GND on the sheet: adder_1_cout
endmodule
