// Logisim project ex4.circ as structural Verilog: 5 circuits, main circuit RotRight
module RotRight (
  input  [15:0] INPUT0,
  input  [3:0] AMOUNT,
  output [15:0] OUTPUT0
);

  wire [15:0] I1, I2, I3, R0, R1, R2, R3;

  rot1 rot1_1 (.in_1(INPUT0), .out_2(R0));
  rot2 rot2_1 (.in_1(I1), .out_2(R1));
  rot4 rot4_1 (.in_1(I2), .out_2(R2));
  rot8 rot8_1 (.in_1(I3), .out_2(R3));
  Multiplexer #(.width(16), .select(1), .enable("false")) multiplexer_1 (
    .in0(INPUT0), .in1(R0), .out(I1), .sel(AMOUNT[0]));
  Multiplexer #(.width(16), .select(1), .enable("false")) multiplexer_2 (.in0(I1), .in1(R1), .out(I2), .sel(AMOUNT[1]));
  Multiplexer #(.width(16), .select(1), .enable("false")) multiplexer_3 (.in0(I2), .in1(R2), .out(I3), .sel(AMOUNT[2]));
  Multiplexer #(.width(16), .select(1), .enable("false")) multiplexer_4 (
    .in0(I3), .in1(R3), .out(OUTPUT0), .sel(AMOUNT[3]));

  // Other names for the same wires on the sheet: q0 = AMOUNT[0]; q1 = AMOUNT[1]; q2 = AMOUNT[2]; q3 = AMOUNT[3];
  //   I0[15:0] = INPUT0; I4[15:0] = OUTPUT0
endmodule

module rot1 (
  input  [15:0] in_1,
  output [15:0] out_2
);


  assign out_2 = {in_1[0], in_1[15:1]};

  // Other names for the same wires on the sheet: b1 = in_1[1]; IN[15:0] = in_1; OUT[15:0] = {in_1[0], in_1[15:1]};
  //   b2 = in_1[2]; b3 = in_1[3]; b4 = in_1[4]; b5 = in_1[5]; b6 = in_1[6]; b7 = in_1[7]; b8 = in_1[8]; b9 = in_1[9];
  //   b10 = in_1[10]; b11 = in_1[11]; b12 = in_1[12]; b13 = in_1[13]; b14 = in_1[14]; b15 = in_1[15]; b0 = in_1[0]
endmodule

module rot2 (
  input  [15:0] in_1,
  output [15:0] out_2
);


  assign out_2 = {in_1[1:0], in_1[15:2]};

  // Other names for the same wires on the sheet: b2 = in_1[2]; IN[15:0] = in_1; OUT[15:0] = {in_1[1:0], in_1[15:2]};
  //   b3 = in_1[3]; b4 = in_1[4]; b5 = in_1[5]; b6 = in_1[6]; b7 = in_1[7]; b8 = in_1[8]; b9 = in_1[9];
  //   b10 = in_1[10]; b11 = in_1[11]; b12 = in_1[12]; b13 = in_1[13]; b14 = in_1[14]; b15 = in_1[15]; b0 = in_1[0];
  //   b1 = in_1[1]
endmodule

module rot4 (
  input  [15:0] in_1,
  output [15:0] out_2
);


  assign out_2 = {in_1[3:0], in_1[15:4]};

  // Other names for the same wires on the sheet: b4 = in_1[4]; IN[15:0] = in_1; OUT[15:0] = {in_1[3:0], in_1[15:4]};
  //   b5 = in_1[5]; b6 = in_1[6]; b7 = in_1[7]; b8 = in_1[8]; b9 = in_1[9]; b10 = in_1[10]; b11 = in_1[11];
  //   b12 = in_1[12]; b13 = in_1[13]; b14 = in_1[14]; b15 = in_1[15]; b0 = in_1[0]; b1 = in_1[1]; b2 = in_1[2];
  //   b3 = in_1[3]
endmodule

module rot8 (
  input  [15:0] in_1,
  output [15:0] out_2
);


  assign out_2 = {in_1[7:0], in_1[15:8]};

  // Other names for the same wires on the sheet: b8 = in_1[8]; IN[15:0] = in_1; OUT[15:0] = {in_1[7:0], in_1[15:8]};
  //   b9 = in_1[9]; b10 = in_1[10]; b11 = in_1[11]; b12 = in_1[12]; b13 = in_1[13]; b14 = in_1[14]; b15 = in_1[15];
  //   b0 = in_1[0]; b1 = in_1[1]; b2 = in_1[2]; b3 = in_1[3]; b4 = in_1[4]; b5 = in_1[5]; b6 = in_1[6]; b7 = in_1[7]
endmodule
