// Logisim project ex1.circ as structural Verilog: 1 circuit, main circuit generate_immediate
module generate_immediate (
  input  [31:0] INSTRUCTION,
  output [31:0] IMMEDIATE
);


  assign IMMEDIATE = {{21{INSTRUCTION[31]}}, INSTRUCTION[30:25], INSTRUCTION[11:7]};

  // Other names for the same wires on the sheet: i7 = INSTRUCTION[7]; i8 = INSTRUCTION[8]; i9 = INSTRUCTION[9];
  //   i10 = INSTRUCTION[10]; i11 = INSTRUCTION[11]; i25 = INSTRUCTION[25]; i26 = INSTRUCTION[26];
  //   i27 = INSTRUCTION[27]; i28 = INSTRUCTION[28]; i29 = INSTRUCTION[29]; i30 = INSTRUCTION[30];
  //   i31 = INSTRUCTION[31]; i0 = INSTRUCTION[0]; i1 = INSTRUCTION[1]; i2 = INSTRUCTION[2]; i3 = INSTRUCTION[3];
  //   i4 = INSTRUCTION[4]; i5 = INSTRUCTION[5]; i6 = INSTRUCTION[6]; i12 = INSTRUCTION[12]; i13 = INSTRUCTION[13];
  //   i14 = INSTRUCTION[14]; i15 = INSTRUCTION[15]; i16 = INSTRUCTION[16]; i17 = INSTRUCTION[17];
  //   i18 = INSTRUCTION[18]; i19 = INSTRUCTION[19]; i20 = INSTRUCTION[20]; i21 = INSTRUCTION[21];
  //   i22 = INSTRUCTION[22]; i23 = INSTRUCTION[23]; i24 = INSTRUCTION[24]
endmodule
