// Logisim project ex4.circ as structural Verilog: 1 circuit, main circuit pipelined
module pipelined (
  input  [7:0] in1,
  input  [7:0] in2,
  input  CLK,
  output [7:0] out1
);

  wire adder_1_cout;
  wire [7:0] delayed_product, product, sum;

  Multiplier #(.width(8)) multiplier_1 (.a(in1), .b(in2), .out(product));  // open: cin, cout
  Register #(.width(8)) product_stage (.D(product), .clk(CLK), .Q(delayed_product));  // open: en, clr
  Adder #(.width(8)) adder_1 (.a(delayed_product), .b(out1), .out(sum), .cout(adder_1_cout));  // open: cin
  Register #(.width(8)) accumulator (.D(sum), .clk(CLK), .Q(out1));  // open: en, clr
  // also tied to GND on the sheet: adder_1_cout
endmodule
